# Fritzing sketch arduino-uss-arduino-11-12 (saved by Fritzing 0.9.3b)

parts:
  hc-sr1 = hc-sr04
  Part1 = Arduino Uno (Rev3) - ICSP

nets:
  VCC: hc-sr1.VCC, Part1.5V
  N1: hc-sr1.Trig, Part1.D11_PWM/MOSI
  N2: hc-sr1.Echo, Part1.D12/MISO
  GND: hc-sr1.GND, Part1.GND

notes:
  ARDUINO - UNO
  HC-SR04
  VCC
  GND
  PIN 11 - TRIG
  PIN 12 - ECHO
